# Fritzing sketch electromagnet_control (saved by Fritzing 0.9.2b)
breadboards: 1

parts:
  Part1 = Arduino Uno (Rev3)
  Q2 = Basic FET N-Channel [part_number=FQP30N06L package="DPak [SMD]"]
  L1 = Solenoid
  D1 = Diode [package=diode-hv]
  R1 = Resistor [tolerance=±5% resistance=2.2k package="0805 [SMD]"]

nets:
  N1: Part1.A3, R1.Pin_1
  GND: Part1.GND, Q2.source
  5V: Part1.5V
  N2: Q2.Gate, R1.Pin_0
  N3: Q2.drain, L1.pin2, D1.A
  12V: L1.pin1, D1.C
